// Logisim project project.circ as structural Verilog: 9 circuits, main circuit main
module main (
);

  wire ALUSrc, AUIPC, Branch, branch_taken, button_1_out, button_3_out, clk, clock_1_out, Lt,
       multiplexer_1_out, not_1_out, not_2_out, ram_1_p2, ram_1_p7, reset, t_ff_1_q, zero;
  wire [2:0] funct3;
  wire [3:0] ALUop, ram_1_p3;
  wire [7:0] datamem_1_write_data_out, datamem_1_write_data_out_2, datamem_1_write_data_out_3,
       datamem_1_write_data_out_4, undriven, undriven_2, undriven_3, undriven_4;
  wire [11:0] control_word;
  wire [15:0] ram_1_p1;
  wire [31:0] alu_result, imm_b, imm_i, imm_j, imm_out, instruction, pc_1_pc_out, PC_plus_4, ram_read_data,
       rs1_val, rs2_val;

  PC pc_1 (
    .branch_taken(branch_taken), .jump(control_word[4]), .jalr(control_word[3]), .imm_b(imm_b),
    .imm_j(imm_j), .clk(clk), .reset(reset), .rs1_val(rs1_val), .imm_i(imm_i), .pc_out(pc_1_pc_out),
    .pc_plus_4(PC_plus_4));
  CU cu_1 (
    .instruction({instruction[31:15], funct3, instruction[11:0]}), .out_2(ALUop), .AUIPC(AUIPC),
    .control_word({control_word[11:7], ALUSrc, Branch, control_word[4:0]}));
  ROM #(.dataWidth(32)) InstMem (.addr(pc_1_pc_out[9:2]), .data({instruction[31:15], funct3, instruction[11:0]}));
  not not_1 (not_1_out, zero);
  not not_2 (not_2_out, Lt);
  // Probe on ram_1_p1
  // Probe on {datamem_1_write_data_out_4, datamem_1_write_data_out_3, datamem_1_write_data_out_2, datamem_1_write_data_out}
  // RAM #(.addrWidth(16), .clearpin("true"), .enables("line"), .line("quad")) ram_1: pin names not known; wires that end beside it: ram_1_p1, ram_1_p2, ram_1_p3[0], ram_1_p3[1], ram_1_p3[2], ram_1_p3[3], ram_1_p7
  Multiplexer #(.select(3)) multiplexer_1 (
    .in0(zero), .in1(not_1_out), .in2(1'b0), .in3(1'b0), .in4(Lt), .in5(not_2_out), .in6(1'b0), .in7(1'b0),
    .out(multiplexer_1_out), .sel(funct3));
  and and_1 (branch_taken, multiplexer_1_out, Branch);
  DataMem datamem_1 (
    .R({reset, 1'bz}), .raw({undriven_4, undriven_3, undriven_2, undriven}), .clk({clk, ram_1_p7}),
    .funct3(funct3), .write_data(rs2_val), .MemWrite({control_word[9], ram_1_p2}), .addr_in(alu_result),
    .write_data_out({datamem_1_write_data_out_4, datamem_1_write_data_out_3, datamem_1_write_data_out_2, datamem_1_write_data_out}),
    .read_data(ram_read_data), .lm(ram_1_p3), .addr(ram_1_p1));  // open: raw_read_data
  // Probe on alu_result
  T_Flip_Flop t_ff_1 (.T(button_1_out), .clk(button_1_out), .Q(t_ff_1_q));  // open: Qn, reset, preset
  Button button_1 (.out(button_1_out));
  Button button_2 (.out(reset));
  Clock clock_1 (.out(clock_1_out));
  Multiplexer multiplexer_2 (.in0(clock_1_out), .in1(button_3_out), .out(clk), .sel(t_ff_1_q));
  Button button_3 (.out(button_3_out));
  // Probe on imm_out
  ImmGen immgen_1 (
    .imm_sel(control_word[2:0]), .instr({instruction[31:15], funct3, instruction[11:0]}), .type_b(imm_b),
    .type_i(imm_i), .type_j(imm_j), .imm_out(imm_out));
  RegFile regfile_1 (
    .rs2_index(instruction[24:20]), .rs1_index(instruction[19:15]), .ram_read_data(ram_read_data),
    .Pc_plus_4(PC_plus_4), .RegWrite(control_word[11]), .Reset(reset), .alu_result(alu_result),
    .rd_index(instruction[11:7]), .clk(clk), .MemtoReg(control_word[8:7]), .rs2_data(rs2_val),
    .rs1_data(rs1_val));
  // Probe on control_word[2:0]
  ALU alu_1 (
    .ALUop(ALUop), .PC_plus_4(PC_plus_4), .rs1_val(rs1_val), .AUIPC(AUIPC), .ALUSrc(ALUSrc),
    .imm_out(imm_out), .rs2_val(rs2_val), .Result(alu_result), .zero(zero), .Lt(Lt));  // open: Ltu

  // Other names for the same wires on the sheet: immSel[2:0] = control_word[2:0]; jalr = control_word[3];
  //   jal = control_word[4]; control_word[6:5] = {ALUSrc, Branch}; MemToReg[1:0] = control_word[8:7];
  //   MemWrite = control_word[9]; MemRead = control_word[10]; RegWrite = control_word[11];
  //   rd_index[4:0] = instruction[11:7]; instruction[14:12] = funct3; rs1_index[4:0] = instruction[19:15];
  //   rs2_index[4:0] = instruction[24:20]

  // Notes on the sheet:
  //   contents of InstMem (hex, n*v repeats v):
  //   500093 fff00113 300193 213 293 313 393 413 493 17517 c50513 10c463 100213 20d463 200293 10d463
  //   300313 10e463 400393 20f463 500413 fe20c6e3 600493 63
  //   Control Word
  //   bit 11 (RegWrite)
  //   bit 10 (MemRead)
  //   bit 9 (MemWrite)
  //   bits 8..7 (MemToReg[1:0])
  //   bit 6 (ALUSrc)
  //   bit 5 (Branch)
  //   bit 4 (Jump(JAL))
  //   bit 3 (Jalr)
  //   bits 2..0 (ImmSel[2:0])
endmodule

module PC (
  input  [31:0] imm_b,
  input  [31:0] imm_j,
  input  [31:0] rs1_val,
  input  clk,
  input  [31:0] imm_i,
  input  reset,
  input  branch_taken,
  input  jump,
  input  jalr,
  output [31:0] pc_out,
  output [31:0] pc_plus_4
);

  wire [31:0] adder_1_out, adder_3_out, adder_4_out, and_1_out, multiplexer_1_out, multiplexer_2_out,
       multiplexer_3_out;

  Register #(.width(32)) pc_reg (.D(multiplexer_3_out), .en(1'b1), .clk(clk), .Q(pc_out), .clr(reset));
  Adder #(.width(32)) adder_1 (.a(rs1_val), .b(imm_i), .out(adder_1_out));  // open: cin, cout
  Adder #(.width(32)) adder_2 (.a(pc_out), .b(32'h4), .out(pc_plus_4));  // open: cin, cout
  Adder #(.width(32)) adder_3 (.a(pc_out), .b(imm_b), .out(adder_3_out));  // open: cin, cout
  Adder #(.width(32)) adder_4 (.a(pc_out), .b(imm_j), .out(adder_4_out));  // open: cin, cout
  assign and_1_out = adder_1_out & 32'hfffffffe;  // AND_Gate and_1, 32 bits wide
  Multiplexer #(.width(32)) multiplexer_1 (
    .in0(pc_plus_4), .in1(adder_3_out), .out(multiplexer_1_out), .sel(branch_taken));
  Multiplexer #(.width(32)) multiplexer_2 (
    .in0(multiplexer_1_out), .in1(adder_4_out), .out(multiplexer_2_out), .sel(jump));
  Multiplexer #(.width(32)) multiplexer_3 (
    .in0(multiplexer_2_out), .in1(and_1_out), .out(multiplexer_3_out), .sel(jalr));

  // Notes on the sheet:
  //   pc_next
endmodule

module InstMem (
  input  [7:0] in_1,
  output [31:0] out_2
);

  ROM #(.dataWidth(32)) rom_1 (.addr(in_1), .data(out_2));

  // Notes on the sheet:
  //   contents of rom_1 (hex, n*v repeats v):
  //   500093 a00113 2081b3 302023 2203
endmodule

module ImmGen (
  input  [31:0] instr,
  input  [2:0] imm_sel,
  output [31:0] type_i,
  output [31:0] imm_out,
  output [31:0] type_b,
  output [31:0] type_j
);

  wire [31:0] bit_extender_1_out;

  assign bit_extender_1_out = {{20{instr[31]}}, {instr[31:25], instr[11:7]}};  // Bit_Extender bit_extender_1
  assign type_i = {{20{instr[31]}}, instr[31:20]};  // Bit_Extender bit_extender_2
  assign type_b = {{19{instr[31]}}, {instr[31], instr[7], instr[30:25], instr[11:8], 1'b0}};  // Bit_Extender bit_extender_3
  assign type_j = {{11{instr[31]}}, {instr[31], instr[19:12], instr[20], instr[30:21], 1'b0}};  // Bit_Extender bit_extender_4
  Multiplexer #(.select(3), .width(32)) multiplexer_1 (
    .in0(type_i), .in1(bit_extender_1_out), .in2(type_b), .in3({instr[31:12], {12{1'b0}}}), .in4(type_j),
    .out(imm_out), .sel(imm_sel));  // open: in5, in6, in7

  // Other names for the same wires on the sheet: p11_8[3:0] = instr[11:8]; p7 = instr[7]; p30_21[9:0] = instr[30:21];
  //   p31_12[19:0] = instr[31:12]; p30_25[5:0] = instr[30:25]; p20 = instr[20]; p19_12[7:0] = instr[19:12];
  //   p31 = instr[31]; p0 = instr[0]

  // Notes on the sheet:
  //   type-s
  //   type-i
  //   type-B
  //   type-u
  //   type-j
endmodule

module RegFile (
  input  [31:0] alu_result,
  input  [31:0] ram_read_data,
  input  [31:0] Pc_plus_4,
  input  [1:0] MemtoReg,
  input  clk,
  input  RegWrite,
  input  Reset,
  input  [4:0] rd_index,
  input  [4:0] rs1_index,
  input  [4:0] rs2_index,
  output [31:0] rs1_data,
  output [31:0] rs2_data
);

  wire demultiplexer_1_out0, demultiplexer_1_out1, demultiplexer_1_out2, demultiplexer_1_out3;
  wire [7:0] demultiplexer_2_out0, demultiplexer_3_out0, demultiplexer_4_out0, demultiplexer_5_out0;
  wire [31:0] write_data, x1_ra_q, x2_sp_q, x3_gp_q, x4_tp_q, x5_t0_q, x6_t1_q, x7_t2_q, x8_s0_q, x9_s1_q,
       x10_a0_q, x11_a1_q, x12_a2_q, x13_a3_q, x14_a4_q, x15_a5_q, x16_a6_q, x17_a7_q, x18_s2_q, x19_s3_q,
       x20_s4_q, x21_s5_q, x22_s6_q, x23_s7_q, x24_s8_q, x25_s9_q, x26_s10_q, x27_s11_q, x28_t3_q, x29_t4_q,
       x30_t5_q, x31_t6_q;

  Demultiplexer #(.select(2)) demultiplexer_1 (
    .out0(demultiplexer_1_out0), .out1(demultiplexer_1_out1), .out2(demultiplexer_1_out2),
    .out3(demultiplexer_1_out3), .in(RegWrite), .sel(rd_index[4:3]));
  Multiplexer #(.select(2), .width(32)) multiplexer_1 (
    .in0(alu_result), .in1(ram_read_data), .in2(Pc_plus_4), .in3({32{1'b0}}), .out(write_data), .sel(MemtoReg));
  // Probe on write_data
  Demultiplexer #(.select(3)) demultiplexer_2 (
    .out0(demultiplexer_2_out0[0]), .out1(demultiplexer_2_out0[1]), .out2(demultiplexer_2_out0[2]),
    .out3(demultiplexer_2_out0[3]), .out4(demultiplexer_2_out0[4]), .out5(demultiplexer_2_out0[5]),
    .out6(demultiplexer_2_out0[6]), .out7(demultiplexer_2_out0[7]), .in(demultiplexer_1_out0),
    .sel(rd_index[2:0]));
  Demultiplexer #(.select(3)) demultiplexer_3 (
    .out0(demultiplexer_3_out0[0]), .out1(demultiplexer_3_out0[1]), .out2(demultiplexer_3_out0[2]),
    .out3(demultiplexer_3_out0[3]), .out4(demultiplexer_3_out0[4]), .out5(demultiplexer_3_out0[5]),
    .out6(demultiplexer_3_out0[6]), .out7(demultiplexer_3_out0[7]), .in(demultiplexer_1_out1),
    .sel(rd_index[2:0]));
  Demultiplexer #(.select(3)) demultiplexer_4 (
    .out0(demultiplexer_4_out0[0]), .out1(demultiplexer_4_out0[1]), .out2(demultiplexer_4_out0[2]),
    .out3(demultiplexer_4_out0[3]), .out4(demultiplexer_4_out0[4]), .out5(demultiplexer_4_out0[5]),
    .out6(demultiplexer_4_out0[6]), .out7(demultiplexer_4_out0[7]), .in(demultiplexer_1_out2),
    .sel(rd_index[2:0]));
  Demultiplexer #(.select(3)) demultiplexer_5 (
    .out0(demultiplexer_5_out0[0]), .out1(demultiplexer_5_out0[1]), .out2(demultiplexer_5_out0[2]),
    .out3(demultiplexer_5_out0[3]), .out4(demultiplexer_5_out0[4]), .out5(demultiplexer_5_out0[5]),
    .out6(demultiplexer_5_out0[6]), .out7(demultiplexer_5_out0[7]), .in(demultiplexer_1_out3),
    .sel(rd_index[2:0]));
  Register #(.width(32)) x8_s0 (.D(write_data), .en(demultiplexer_3_out0[0]), .clk(clk), .Q(x8_s0_q), .clr(Reset));
  Register #(.width(32)) x16_a6 (.D(write_data), .en(demultiplexer_4_out0[0]), .clk(clk), .Q(x16_a6_q), .clr(Reset));
  Register #(.width(32)) x24_s8 (.D(write_data), .en(demultiplexer_5_out0[0]), .clk(clk), .Q(x24_s8_q), .clr(Reset));
  Register #(.width(32)) x1_ra (.D(write_data), .en(demultiplexer_2_out0[1]), .clk(clk), .Q(x1_ra_q), .clr(Reset));
  Register #(.width(32)) x9_s1 (.D(write_data), .en(demultiplexer_3_out0[1]), .clk(clk), .Q(x9_s1_q), .clr(Reset));
  Register #(.width(32)) x17_a7 (.D(write_data), .en(demultiplexer_4_out0[1]), .clk(clk), .Q(x17_a7_q), .clr(Reset));
  Register #(.width(32)) x25_s9 (.D(write_data), .en(demultiplexer_5_out0[1]), .clk(clk), .Q(x25_s9_q), .clr(Reset));
  Register #(.width(32)) x2_sp (.D(write_data), .en(demultiplexer_2_out0[2]), .clk(clk), .Q(x2_sp_q), .clr(Reset));
  Register #(.width(32)) x10_a0 (.D(write_data), .en(demultiplexer_3_out0[2]), .clk(clk), .Q(x10_a0_q), .clr(Reset));
  Register #(.width(32)) x18_s2 (.D(write_data), .en(demultiplexer_4_out0[2]), .clk(clk), .Q(x18_s2_q), .clr(Reset));
  Register #(.width(32)) x26_s10 (.D(write_data), .en(demultiplexer_5_out0[2]), .clk(clk), .Q(x26_s10_q), .clr(Reset));
  Register #(.width(32)) x3_gp (.D(write_data), .en(demultiplexer_2_out0[3]), .clk(clk), .Q(x3_gp_q), .clr(Reset));
  Register #(.width(32)) x11_a1 (.D(write_data), .en(demultiplexer_3_out0[3]), .clk(clk), .Q(x11_a1_q), .clr(Reset));
  Register #(.width(32)) x19_s3 (.D(write_data), .en(demultiplexer_4_out0[3]), .clk(clk), .Q(x19_s3_q), .clr(Reset));
  Register #(.width(32)) x27_s11 (.D(write_data), .en(demultiplexer_5_out0[3]), .clk(clk), .Q(x27_s11_q), .clr(Reset));
  Register #(.width(32)) x4_tp (.D(write_data), .en(demultiplexer_2_out0[4]), .clk(clk), .Q(x4_tp_q), .clr(Reset));
  Register #(.width(32)) x12_a2 (.D(write_data), .en(demultiplexer_3_out0[4]), .clk(clk), .Q(x12_a2_q), .clr(Reset));
  Register #(.width(32)) x20_s4 (.D(write_data), .en(demultiplexer_4_out0[4]), .clk(clk), .Q(x20_s4_q), .clr(Reset));
  Register #(.width(32)) x28_t3 (.D(write_data), .en(demultiplexer_5_out0[4]), .clk(clk), .Q(x28_t3_q), .clr(Reset));
  Register #(.width(32)) x5_t0 (.D(write_data), .en(demultiplexer_2_out0[5]), .clk(clk), .Q(x5_t0_q), .clr(Reset));
  Register #(.width(32)) x13_a3 (.D(write_data), .en(demultiplexer_3_out0[5]), .clk(clk), .Q(x13_a3_q), .clr(Reset));
  Register #(.width(32)) x21_s5 (.D(write_data), .en(demultiplexer_4_out0[5]), .clk(clk), .Q(x21_s5_q), .clr(Reset));
  Register #(.width(32)) x29_t4 (.D(write_data), .en(demultiplexer_5_out0[5]), .clk(clk), .Q(x29_t4_q), .clr(Reset));
  Register #(.width(32)) x6_t1 (.D(write_data), .en(demultiplexer_2_out0[6]), .clk(clk), .Q(x6_t1_q), .clr(Reset));
  Register #(.width(32)) x14_a4 (.D(write_data), .en(demultiplexer_3_out0[6]), .clk(clk), .Q(x14_a4_q), .clr(Reset));
  Register #(.width(32)) x22_s6 (.D(write_data), .en(demultiplexer_4_out0[6]), .clk(clk), .Q(x22_s6_q), .clr(Reset));
  Register #(.width(32)) x30_t5 (.D(write_data), .en(demultiplexer_5_out0[6]), .clk(clk), .Q(x30_t5_q), .clr(Reset));
  Register #(.width(32)) x7_t2 (.D(write_data), .en(demultiplexer_2_out0[7]), .clk(clk), .Q(x7_t2_q), .clr(Reset));
  Register #(.width(32)) x15_a5 (.D(write_data), .en(demultiplexer_3_out0[7]), .clk(clk), .Q(x15_a5_q), .clr(Reset));
  Register #(.width(32)) x23_s7 (.D(write_data), .en(demultiplexer_4_out0[7]), .clk(clk), .Q(x23_s7_q), .clr(Reset));
  Register #(.width(32)) x31_t6 (.D(write_data), .en(demultiplexer_5_out0[7]), .clk(clk), .Q(x31_t6_q), .clr(Reset));
  Multiplexer #(.select(5), .width(32)) multiplexer_2 (
    .in0({32{1'b0}}), .in1(x1_ra_q), .in2(x2_sp_q), .in3(x3_gp_q), .in4(x4_tp_q), .in5(x5_t0_q),
    .in6(x6_t1_q), .in7(x7_t2_q), .in8(x8_s0_q), .in9(x9_s1_q), .in10(x10_a0_q), .in11(x11_a1_q),
    .in12(x12_a2_q), .in13(x13_a3_q), .in14(x14_a4_q), .in15(x15_a5_q), .in16(x16_a6_q), .in17(x17_a7_q),
    .in18(x18_s2_q), .in19(x19_s3_q), .in20(x20_s4_q), .in21(x21_s5_q), .in22(x22_s6_q), .in23(x23_s7_q),
    .in24(x24_s8_q), .in25(x25_s9_q), .in26(x26_s10_q), .in27(x27_s11_q), .in28(x28_t3_q), .in29(x29_t4_q),
    .in30(x30_t5_q), .in31(x31_t6_q), .out(rs1_data), .sel(rs1_index));
  Multiplexer #(.select(5), .width(32)) multiplexer_3 (
    .in0({32{1'b0}}), .in1(x1_ra_q), .in2(x2_sp_q), .in3(x3_gp_q), .in4(x4_tp_q), .in5(x5_t0_q),
    .in6(x6_t1_q), .in7(x7_t2_q), .in8(x8_s0_q), .in9(x9_s1_q), .in10(x10_a0_q), .in11(x11_a1_q),
    .in12(x12_a2_q), .in13(x13_a3_q), .in14(x14_a4_q), .in15(x15_a5_q), .in16(x16_a6_q), .in17(x17_a7_q),
    .in18(x18_s2_q), .in19(x19_s3_q), .in20(x20_s4_q), .in21(x21_s5_q), .in22(x22_s6_q), .in23(x23_s7_q),
    .in24(x24_s8_q), .in25(x25_s9_q), .in26(x26_s10_q), .in27(x27_s11_q), .in28(x28_t3_q), .in29(x29_t4_q),
    .in30(x30_t5_q), .in31(x31_t6_q), .out(rs2_data), .sel(rs2_index));

  // Other names for the same wires on the sheet: R = Reset; rd_index2_0[2:0] = rd_index[2:0];
  //   rd_index4_3[1:0] = rd_index[4:3]

  // Notes on the sheet:
  //   x0_zero
endmodule

module ALU (
  input  [31:0] rs1_val,
  input  [31:0] rs2_val,
  input  [31:0] PC_plus_4,
  input  AUIPC,
  input  [31:0] imm_out,
  input  ALUSrc,
  input  [3:0] ALUop,
  output [31:0] Result,
  output zero,
  output Lt,
  output Ltu
);

  wire [31:0] adder_1_out, and_1_out, bit_extender_1_out, bit_extender_2_out, or_1_out, rs1_val_t,
       rs2_or_imm, shifter_1_out, shifter_2_out, shifter_3_out, subtractor_1_out, subtractor_2_out, xor_1_out;

  Subtractor #(.width(32)) subtractor_1 (.a(PC_plus_4), .b(32'h4), .out(subtractor_1_out));  // open: bin, bout
  Multiplexer #(.width(32)) multiplexer_1 (.in0(rs1_val), .in1(subtractor_1_out), .out(rs1_val_t), .sel(AUIPC));
  Multiplexer #(.width(32)) multiplexer_2 (.in0(rs2_val), .in1(imm_out), .out(rs2_or_imm), .sel(ALUSrc));
  Comparator #(.width(32)) comparator_1 (.a(rs1_val_t), .b(rs2_or_imm), .lt(Lt));  // open: gt, eq
  Comparator #(.mode("unsigned"), .width(32)) comparator_2 (.a(rs1_val_t), .b(rs2_or_imm), .lt(Ltu));  // open: gt, eq
  Adder #(.width(32)) adder_1 (.a(rs1_val_t), .b(rs2_or_imm), .out(adder_1_out));  // open: cin, cout
  Subtractor #(.width(32)) subtractor_2 (.a(rs1_val_t), .b(rs2_or_imm), .out(subtractor_2_out));  // open: bin, bout
  Shifter #(.width(32)) shifter_1 (.in(rs1_val_t), .\dist (rs2_or_imm[4:0]), .out(shifter_1_out));
  assign bit_extender_1_out = {{31{1'b0}}, Lt};  // Bit_Extender bit_extender_1
  assign bit_extender_2_out = {{31{1'b0}}, Ltu};  // Bit_Extender bit_extender_2
  assign xor_1_out = rs1_val_t ^ rs2_or_imm;  // XOR_Gate xor_1, 32 bits wide
  Shifter #(.shift("lr"), .width(32)) shifter_2 (.in(rs1_val_t), .\dist (rs2_or_imm[4:0]), .out(shifter_2_out));
  Shifter #(.shift("ar"), .width(32)) shifter_3 (.in(rs1_val_t), .\dist (rs2_or_imm[4:0]), .out(shifter_3_out));
  assign or_1_out = rs1_val_t | rs2_or_imm;  // OR_Gate or_1, 32 bits wide
  assign and_1_out = rs1_val_t & rs2_or_imm;  // AND_Gate and_1, 32 bits wide
  Multiplexer #(.select(4), .width(32)) multiplexer_3 (
    .in0(adder_1_out), .in1(subtractor_2_out), .in2(shifter_1_out), .in3(bit_extender_1_out),
    .in4(bit_extender_2_out), .in5(xor_1_out), .in6(shifter_2_out), .in7(shifter_3_out), .in8(or_1_out),
    .in9(and_1_out), .in10(rs2_or_imm), .in11(rs1_val_t), .out(Result), .sel(ALUop));  // open: in12, in13, in14, in15
  Comparator #(.width(32)) comparator_3 (.a(Result), .b({32{1'b0}}), .eq(zero));  // open: gt, lt

  // Other names for the same wires on the sheet: shamt[4:0] = rs2_or_imm[4:0]

  // Notes on the sheet:
  //   SLT-0011
  //   SLTU-0100
  //   XOR-0101
  //   SRL-0110
  //   SRA-0111
  //   OR-1000
  //   AND-1001
  //   COPY-B-1010
  //   PASS-A-1011
  //   ADD-0000
  //   SUB-0001
  //   SLL-0010
endmodule

module CU (
  input  [31:0] instruction,
  output [3:0] out_2,
  output [11:0] control_word,
  output AUIPC
);

  wire [1:0] word_data;

  // Probe on instruction[6:0]
  // Probe on instruction[14:12]
  // Probe on instruction[30]
  Comparator #(.width(7)) comparator_1 (.a(instruction[6:0]), .b(7'b0010111), .eq(AUIPC));  // open: gt, lt
  // Probe on instruction[6:0]
  ROM #(.addrWidth(7), .dataWidth(14)) word (.addr(instruction[6:0]), .data({control_word, word_data}));
  // Probe on {control_word, word_data}
  // Probe on word_data
  ROM #(.addrWidth(6), .dataWidth(4)) ALUControl (
    .addr({word_data, instruction[30], instruction[14:12]}), .data(out_2));

  // Other names for the same wires on the sheet: funct3[2:0] = instruction[14:12]; funct7_bit = instruction[30];
  //   opcode[6:0] = instruction[6:0]

  // Notes on the sheet:
  //   contents of word (hex, n*v repeats v):
  //   0 0 0 3303 15*0 2101 0 0 0 210c 11*0 905 15*0 2000 0 0 0 210f 43*0 8a 0 0 0 2520 7*0 2451
  //   contents of ALUControl (hex, n*v repeats v):
  //   0 2 3 4 5 6 8 0 1 2 3 4 5 7 8 9 0 2 3 4 5 6 8 9 0 2 3 4 5 7 8 9 16*1
endmodule

module DataMem (
  input  [31:0] addr_in,
  input  Reset,
  input  clk,
  input  [31:0] raw,
  input  MemWrite,
  input  [2:0] funct3,
  input  [31:0] write_data,
  output R,
  output ck,
  output [15:0] addr,
  output [31:0] raw_read_data,
  output mw,
  output [31:0] read_data,
  output [3:0] lm,
  output [31:0] write_data_out
);

  wire [3:0] sb_mask, sh_mask;
  wire [4:0] bit_extender_1_out, shift_amt;
  wire [31:0] LB, LBU, LH, LHU, mid_result, shifter_3_out, shifter_4_out, shifter_5_out;

  Multiplexer #(.select(2), .width(4)) multiplexer_1 (
    .in0(4'b0001), .in1(4'b0010), .in2(4'b0100), .in3(4'b1000), .out(sb_mask), .sel(addr_in[1:0]));
  Multiplexer #(.select(2), .width(4)) multiplexer_2 (
    .in0(4'b0011), .in2(4'b1100), .out(sh_mask), .sel(addr_in[1:0]));  // open: in1, in3
  Multiplexer #(.select(3), .width(4)) multiplexer_3 (
    .in0(sb_mask), .in1(sh_mask), .in2(4'b1111), .out(lm), .sel(funct3));  // open: in3, in4, in5, in6, in7
  Shifter #(.width(32)) shifter_1 (.in(write_data), .\dist (shift_amt), .out(mid_result));
  Multiplexer #(.select(3), .width(32)) multiplexer_4 (
    .in0(mid_result), .in1(mid_result), .in2(write_data), .out(write_data_out), .sel(funct3));  // open: in3, in4, in5, in6, in7
  assign bit_extender_1_out = {{3{1'b0}}, addr_in[1:0]};  // Bit_Extender bit_extender_1
  Shifter #(.width(5)) shifter_2 (.in(bit_extender_1_out), .\dist (3'b011), .out(shift_amt));
  Shifter #(.shift("lr"), .width(32)) shifter_3 (.in(raw), .\dist (shift_amt), .out(shifter_3_out));
  Shifter #(.width(32)) shifter_4 (.in(LBU), .\dist (5'b11000), .out(shifter_4_out));
  Shifter #(.width(32)) shifter_5 (.in(LHU), .\dist (5'b10000), .out(shifter_5_out));
  assign LBU = 32'hff & shifter_3_out;  // AND_Gate and_1, 32 bits wide
  assign LHU = 32'hffff & shifter_3_out;  // AND_Gate and_2, 32 bits wide
  Shifter #(.shift("ar"), .width(32)) shifter_6 (.in(shifter_4_out), .\dist (5'b11000), .out(LB));
  Shifter #(.shift("ar"), .width(32)) shifter_7 (.in(shifter_5_out), .\dist (5'b10000), .out(LH));
  Multiplexer #(.select(3), .width(32)) multiplexer_5 (
    .in0(LB), .in1(LH), .in2(raw), .in3({32{1'b0}}), .in4(LBU), .in5(LHU), .in6({32{1'b0}}),
    .in7({32{1'b0}}), .out(read_data), .sel(funct3));

  assign addr = {addr_in[15:2], 2'b00};
  assign ck = clk;
  assign mw = MemWrite;
  assign R = Reset;
  assign raw_read_data = raw;

  // Other names for the same wires on the sheet: offset[1:0] = addr_in[1:0]; f3[2:0] = funct3; LW[31:0] = raw
endmodule

module test (
);

  wire ALUSrc, Branch, branch_taken, button_1_out, button_3_out, clk, clock_1_out, Lt, multiplexer_1_out,
       not_1_out, not_2_out, ram_1_p1, ram_1_p2, ram_1_p3, reset, t_ff_1_q, zero;
  wire [2:0] funct3;
  wire [3:0] ALUop, datamem_1_p7;
  wire [7:0] datamem_1_p17, datamem_1_p17_2, datamem_1_p17_3, datamem_1_p17_4;
  wire [11:0] control_word;
  wire [31:0] alu_result, datamem_1_p4, imm_b, imm_i, imm_j, imm_out, instruction, pc_1_pc_out, PC_plus_4,
       ram_read_data, rs1_val, rs2_val;

  PC pc_1 (
    .branch_taken(branch_taken), .jump(control_word[4]), .jalr(control_word[3]), .imm_b(imm_b),
    .imm_j(imm_j), .clk(clk), .reset(reset), .rs1_val(rs1_val), .imm_i(imm_i), .pc_out(pc_1_pc_out),
    .pc_plus_4(PC_plus_4));
  CU cu_1 (
    .instruction({instruction[31:15], funct3, instruction[11:0]}), .out_2(ALUop),
    .control_word({control_word[11:7], ALUSrc, Branch, control_word[4:0]}));  // open: AUIPC
  ROM #(.dataWidth(32)) InstMem (.addr(pc_1_pc_out[9:2]), .data({instruction[31:15], funct3, instruction[11:0]}));
  not not_1 (not_1_out, zero);
  not not_2 (not_2_out, Lt);
  // RAM #(.addrWidth(16), .enables("line"), .line("quad")) ram_1: pin names not known; wires that end beside it: ram_1_p1, ram_1_p2, ram_1_p3
  Multiplexer #(.select(3)) multiplexer_1 (
    .in0(zero), .in1(not_1_out), .in2(1'b0), .in3(1'b0), .in4(Lt), .in5(not_2_out), .in6(1'b0), .in7(1'b0),
    .out(multiplexer_1_out), .sel(funct3));
  and and_1 (branch_taken, multiplexer_1_out, Branch);
  // DataMem datamem_1: pin names not known; wires that end beside it: control_word[9], control_word[10], rs2_val, datamem_1_p4, ram_1_p1, ram_1_p2, datamem_1_p7, ram_1_p3, datamem_1_p7[0], datamem_1_p7[1], datamem_1_p7[2], datamem_1_p7[3], reset, alu_result, clk, funct3, {datamem_1_p17_4, datamem_1_p17_3, datamem_1_p17_2, datamem_1_p17}, ram_read_data
  // Probe on alu_result
  T_Flip_Flop t_ff_1 (.T(button_1_out), .clk(button_1_out), .Q(t_ff_1_q));  // open: Qn, reset, preset
  Button button_1 (.out(button_1_out));
  Button button_2 (.out(reset));
  Clock clock_1 (.out(clock_1_out));
  Multiplexer multiplexer_2 (.in0(clock_1_out), .in1(button_3_out), .out(clk), .sel(t_ff_1_q));
  Button button_3 (.out(button_3_out));
  // Probe on imm_out
  ImmGen immgen_1 (
    .imm_sel(control_word[2:0]), .instr({instruction[31:15], funct3, instruction[11:0]}), .type_b(imm_b),
    .type_i(imm_i), .type_j(imm_j), .imm_out(imm_out));
  RegFile regfile_1 (
    .rs2_index(instruction[24:20]), .rs1_index(instruction[19:15]), .ram_read_data(ram_read_data),
    .Pc_plus_4(PC_plus_4), .RegWrite(control_word[11]), .Reset(reset), .alu_result(alu_result),
    .rd_index(instruction[11:7]), .clk(clk), .MemtoReg(control_word[8:7]), .rs2_data(rs2_val),
    .rs1_data(rs1_val));
  // Probe on control_word[2:0]
  ALU alu_1 (
    .ALUop(ALUop), .rs1_val(rs1_val), .ALUSrc(ALUSrc), .imm_out(imm_out), .rs2_val(rs2_val),
    .Result(alu_result), .zero(zero), .Lt(Lt));  // open: PC_plus_4, AUIPC, Ltu

  // Other names for the same wires on the sheet: immSel[2:0] = control_word[2:0]; jalr = control_word[3];
  //   jal = control_word[4]; control_word[6:5] = {ALUSrc, Branch}; MemToReg[1:0] = control_word[8:7];
  //   MemWrite = control_word[9]; MemRead = control_word[10]; RegWrite = control_word[11];
  //   rd_index[4:0] = instruction[11:7]; instruction[14:12] = funct3; rs1_index[4:0] = instruction[19:15];
  //   rs2_index[4:0] = instruction[24:20]

  // Notes on the sheet:
  //   contents of InstMem (hex, n*v repeats v):
  //   10000093 11223537 44450513 a0a023 ab00613 861613 cd60613 c09223 c09323 aa00213 408423 bb00213 4084a3
  //   cc00213 408523 dd00213 4085a3 63
  //   Control Word
  //   bit 11 (RegWrite)
  //   bit 10 (MemRead)
  //   bit 9 (MemWrite)
  //   bits 8..7 (MemToReg[1:0])
  //   bit 6 (ALUSrc)
  //   bit 5 (Branch)
  //   bit 4 (Jump(JAL))
  //   bit 3 (Jalr)
  //   bits 2..0 (ImmSel[2:0])
endmodule
